# Fritzing sketch ATBRR (saved by Fritzing 0.9.2b)
breadboards: 1

parts:
  Part1 = Arduino Due (Rev2b)
  Raspberry_Pi1 = Raspberry Pi 2
  J1 = Basic Servo
  J2 = Basic Servo
  U2 = TCM8240MD [package=tcm8240md]  # not connected
  MD03A1 = Dual VNH2SP30 Motor Driver [part_number=MD03A]
  M2 = DC Motor
  M1 = DC Motor
  BAT1 = BC9VPC [package=bc9vpc]

nets:
  N1: Part1.D17/RX2, Raspberry_Pi1.GPIO14
  N2: Part1.D18/TX1, Raspberry_Pi1.GPIO15
  VCC: Part1.5V, J1.vcc, J2.vcc, MD03A1.+5V_(IN)
  GND: Part1.GND, Raspberry_Pi1.GND, J1.gnd, J2.gnd, MD03A1.GND#138
  N3: Part1.D8_PWM, MD03A1.2INb#142
  N4: Part1.D11_PWM, MD03A1.PWM
  N5: Part1.D12_PWM, MD03A1.1INb
  N6: Part1.D13_PWM, MD03A1.1INa
  N7: Part1.D3_PWM, J1.pulse
  N8: Part1.D5_PWM, J2.pulse
  N9: Part1.D6_PWM, MD03A1.2PWM
  N10: Part1.D7_PWM, MD03A1.2INb#143
  N11: MD03A1.OUT_1A, M2.pin_2
  N12: MD03A1.OUT_1B, M2.pin_1
  N13: MD03A1.OUT_2A, M1.pin_2
  N14: MD03A1.OUT_2B, M1.pin_1
  N15: MD03A1.VIN, BAT1.V+
  N16: MD03A1.GND#151, BAT1.V-

notes:
  Pan
  Tilt
